# Fritzing sketch RaspberryI2Cconnection (saved by Fritzing 0.9.2b)
breadboards: 1

parts:
  Raspberry_Pi1 = Raspberry Pi 2
  Part1 = Adafruit ADS1115 16Bit I2C ADC [part_number="Adafruit #1085"]
  PWM1 = PCA9685 16x12-bit PWM Breakout
  J1 = Basic Servo
  J2 = Basic Servo  # not connected
  BAT1 = 18650 battery holder [package=battery-18650-kit]
  U1 = 2RelayModule
  S1 = Momentary Switch [package=ksa_sealed_tac_switch]

nets:
  N1: Raspberry_Pi1.GPIO2, Part1.SDA, PWM1.no_name_yet#604
  N2: Raspberry_Pi1.GPIO3, Part1.SCL, PWM1.no_name_yet#603
  N3: Raspberry_Pi1.GPIO17, S1.3, S1.4
  N4: Raspberry_Pi1.GPIO19, U1.IN1
  N5: Raspberry_Pi1.GPIO26, U1.IN2
  5V: Raspberry_Pi1.5V, PWM1.no_name_yet#605, U1.VCC
  N6: Part1.AIN0, BAT1.+
  GND: Part1.GND, PWM1.no_name_yet#601, PWM1.no_name_yet#1000, J1.gnd, BAT1.-, U1.GND, S1.1, S1.2
  N7: PWM1.no_name_yet#0, J1.pulse
  N8: PWM1.no_name_yet#100, J1.vcc

notes:
  All RED cables are connected to +5V
  All black cables are connected to ground
  Purple cables are connected to I2C SDA
  Yellow cables are connected to I2C SCL
  Battery cell here is only used to measure voltage, no schematic of power system is displayed

custom parts:
  Adafruit ADS1115 16Bit I2C ADC: For microcontrollers without an analog-to-digital converter or when you want a higher-precision ADC, the ADS1115 provides 16-bit precision at 860 samples/second over I2C. The chip can be configured as 4 single-ended input channels, or two differential channels. As a nice bonus, it even includes a programmable gain amplifier, up to x16, to help boost up smaller single/differential signals to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
  18650 battery holder: 18650 Battery Holder
  2RelayModule: 2 relay arduino module SONGLE SRD05VDC-SL-C
