# Fritzing sketch RpiPower_AllBatteries_PWMServos (saved by Fritzing 0.9.2b)

parts:
  Raspberry_Pi2 = Raspberry Pi B+
  Part1 = Adafruit DC+Stepper Motor HAT [part_number="Adafruit #2348"]
  Part2 = Adafruit ADS1115 16Bit I2C ADC [part_number="Adafruit #1085"]
  U1 = 2RelayModule
  Part4 = PowerBoost 500 Charger
  Part5 = ACS712 Low Current Sensor Board v12
  X1 = USB Connectors [package=usb-microb]
  Part6 = ACS712 Low Current Sensor Board v12
  Part7 = PowerBoost 500 Charger
  BAT1 = 18650 battery holder [package=battery-18650-kit]
  BAT2 = 18650 battery holder [package=battery-18650-kit]
  Part8 = Adafruit ADS1115 16Bit I2C ADC [part_number="Adafruit #1085"]
  Part9 = 16-Channel 12-bit PCA9685 PWM/Servo Driver
  U2 = DC-DC 2-24V Step Up Booster [package=THT]
  Part10 = PowerBoost 500 Charger
  BAT3 = 18650 battery holder [package=battery-18650-kit]
  Part11 = PowerBoost 500 Charger
  BAT4 = 18650 battery holder [package=battery-18650-kit]
  U3 = DC-DC 2-24V Step Up Booster [package=THT]
  J1 = Basic Servo
  J2 = Basic Servo
  J3 = Basic Servo
  J4 = Basic Servo
  S1 = H-Bridge with L298N
  M1 = DC Motor
  M2 = DC Motor
  M3 = DC Motor
  M4 = DC Motor
  M5 = DC Motor
  S4 = Momentary Switch [package=ksa_sealed_tac_switch]
  S5 = Momentary Switch [package=ksa_sealed_tac_switch]
  S6 = Momentary Switch [package=ksa_sealed_tac_switch]
  S7 = Momentary Switch [package=ksa_sealed_tac_switch]
  Power_plug1 = Power plug
  J5 = Basic Servo
  S8 = Momentary Switch [package=ksa_sealed_tac_switch]
  Part12 = ACS712 Low Current Sensor Board v12
  J6 = Basic Servo
  J7 = Basic Servo
  U4 = 2RelayModule  # not connected
  J8 = Basic Servo
  J9 = Basic Servo
  J10 = Basic Servo
  LED1 = LEDs [package=led10mm]  # not connected
  LED2 = LEDs [package=led10mm]  # not connected
  J11 = Basic Servo  # not connected
  J12 = Basic Servo  # not connected
  J13 = Basic Servo  # not connected
  J14 = Basic Servo  # not connected
  J15 = Basic Servo  # not connected
  S9 = Round Pushbutton  # not connected

nets:
  3V3: Raspberry_Pi2.3v3, Raspberry_Pi2.3V3, Part1.3.3V
  N1: Raspberry_Pi2.GPIO2, Part1.SDA, Part2.SDA, Part8.SDA, Part9.SDA
  N2: Raspberry_Pi2.GPIO3, Part1.SCL, Part2.SCL, Part8.SCL, Part9.SCL
  N3: Raspberry_Pi2.GPIO4, Part1.GPIO4
  GND: Raspberry_Pi2.GND, Part1.GND, Part2.ADDR, Part2.GND, U1.GND, Part4.GND, Part5.IP+, Part5.IP-, Part5.GND, X1.GND, Part6.IP-, Part6.GND, Part7.GND, BAT2.-, Part8.GND, Part9.GND, U2.pin2, U2.pin4, Part10.GND, BAT3.-, Part11.GND, BAT4.-, U3.pin4, J1.gnd, J2.gnd, J3.gnd, J4.gnd, S4.3, S5.3, J5.gnd, S8.3, Part12.IP-, Part12.GND, J6.gnd, J7.gnd, J8.gnd, J9.gnd, J10.gnd
  N4: Raspberry_Pi2.GPIO17, Part1.GPIO17
  N5: Raspberry_Pi2.GPIO27, Part1.GPIO27
  N6: Raspberry_Pi2.GPIO22, Part1.GPIO22
  N7: Raspberry_Pi2.GPIO10, Part1.SPI_MOSI
  N8: Raspberry_Pi2.GPIO9, Part1.SPI_MISO
  N9: Raspberry_Pi2.GPIO11, Part1.SPI_SCLK
  N10: Raspberry_Pi2.ID_SD, Part1.EEDATA
  N11: Raspberry_Pi2.GPIO5, Part1.GPIO5, S7.1
  N12: Raspberry_Pi2.GPIO6, Part1.GPIO6, S4.1
  N13: Raspberry_Pi2.GPIO13, Part1.GPIO13, S1.IN4
  N14: Raspberry_Pi2.GPIO19, Part1.GPIO19, S1.IN1
  N15: Raspberry_Pi2.GPIO26, Part1.GPIO26, S1.IN2
  N16: Raspberry_Pi2.GPIO21, Part1.GPIO21, U1.IN1
  N17: Raspberry_Pi2.GPIO20, Part1.GPIO20, U1.IN2
  N18: Raspberry_Pi2.GPIO16, Part1.GPIO16, S1.IN3
  N19: Raspberry_Pi2.GPIO12, Part1.GPIO12, S5.1
  N20: Raspberry_Pi2.ID_SC, Part1.EECLK
  N21: Raspberry_Pi2.GPIO7, Part1.SPI_CE1
  N22: Raspberry_Pi2.GPIO8, Part1.SPI_CE0
  N23: Raspberry_Pi2.GPIO25, Part1.GPIO25, S6.1
  N24: Raspberry_Pi2.GPIO24, Part1.GPIO24, S8.1
  N25: Raspberry_Pi2.GPIO23, Part1.GPIO23
  N26: Raspberry_Pi2.GPIO18, Part1.GPIO18
  N27: Raspberry_Pi2.GPIO15, Part1.RXD
  N28: Raspberry_Pi2.GPIO14, Part1.TXD
  5V: Raspberry_Pi2.5V, Part1.5.0V, Part2.VDD, U1.VCC, Part5.5V, Part6.5V, Part8.ADDR, Part8.VDD, Part9.VCC, Part12.5V
  N29: Part1.M2A, M4.pin_1
  N30: Part1.M2B, M4.pin_2
  N31: Part1.M1B, M3.pin_1
  N32: Part1.M1A, M3.pin_2
  N33: Part1.M3B, M5.pin_1
  N34: Part1.M3A, M5.pin_2
  N35: Part1.VMOTOR, U2.pin1
  N36: Part2.AIN3, Part12.VO
  N37: Part2.AIN2, Part4.VBAT, BAT1.+
  N38: Part2.AIN1, Part6.VO
  N39: Part2.AIN0, Part5.VO
  N40: U1.NC1, U1.NC2, X1.VBUS
  N41: U1.MAIN1, Part4.USB
  N42: U1.NO2, Part4.5.0V, Part7.5.0V, Part10.5.0V, Part11.5.0V, Power_plug1.GND
  N43: Part6.IP+, BAT1.-
  N44: Part7.VBAT, BAT2.+, Part8.AIN1
  N45: Part7.USB, Part9.PWRIN
  N46: Part8.AIN2, Part11.VBAT, BAT4.+, U3.pin3
  N47: Part8.AIN0, U2.pin3, Part10.VBAT, BAT3.+
  N48: Part9.0, J1.pulse
  VCC: Part9.V+, J1.vcc, J2.vcc, J3.vcc, J4.vcc, J5.vcc, J6.vcc, J7.vcc, J8.vcc, J9.vcc, J10.vcc
  N49: Part9.1, J2.pulse
  N50: Part9.2, J3.pulse
  N51: Part9.3, J4.pulse
  N52: Part9.4, J6.pulse
  N53: Part9.5, J7.pulse
  N54: Part9.6, J9.pulse
  N55: Part9.7, J8.pulse
  N56: Part9.8, J10.pulse
  N57: Part9.9, J5.pulse
  N58: Part9.14, S1.ENB
  N59: Part9.15, S1.ENA
  N60: U3.pin1, S1.12V
  N61: U3.pin2, S1.GND
  N62: S1.M1-01, M1.pin_2
  N63: S1.M1-02, M1.pin_1
  N64: S1.M2-01, M2.pin_2
  N65: S1.M2-02, M2.pin_1
  N66: S4.4, S7.3
  N67: S5.4, S6.3
  N68: Power_plug1.VCC, Part12.IP+

notes:
  Micro USB to power Raspberry Pi
  Analog current sensor
  (current from DS to Charger)
  To the Docking Station (DS) power bus (5V DC)
  DD04CVSB_5V
  Battery charger
  ("UPS" module)
  Analog current sensor
  (current from/to battery)
  12V booster for MOVEMENT motors
  12V booster for the DOCKING motors
  Battery for Raspberry
  Battery for the DOCKING motors
  Battery for MOVEMENT motors
  Battery for SERVO motors (PWM)
  MOVEMENT motors
  DOCKING motors
  ARM Power system
  DOCKING end switches
  NAV camera Servos
  CANtenna Servos
  Light Servos
  Emergency button (TBD)
  Analog current sensor
  (total current from DS)

custom parts:
  Adafruit DC+Stepper Motor HAT: Let your robotic dreams come true with the new DC+Stepper Motor HAT from Adafruit. This Raspberry Pi add-on is perfect for any motion project as it can drive up to 4 DC or 2 Stepper motors with full PWM speed control. Since the Raspberry Pi does not have a lot of PWM pins, we use a fully-dedicated PWM driver chip onboard to both control motor direction and speed. This chip handles all the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
  Adafruit ADS1115 16Bit I2C ADC: For microcontrollers without an analog-to-digital converter or when you want a higher-precision ADC, the ADS1115 provides 16-bit precision at 860 samples/second over I2C. The chip can be configured as 4 single-ended input channels, or two differential channels. As a nice bonus, it even includes a programmable gain amplifier, up to x16, to help boost up smaller single/differential signals to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
  2RelayModule: 2 relay arduino module SONGLE SRD05VDC-SL-C
  PowerBoost 500 Charger: The PowerBoost 500C is a little DC/DC boost converter module that can be powered by any 3.7V LiIon/LiPoly battery, and convert the battery output to 5.2V DC for running your 5V projects. At its heart is a TPS61090 boost converter from TI. This boost converter chip has some really nice extras such as low battery detection, 2A internal switch, synchronous conversion, excellent efficiency, and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
  18650 battery holder: 18650 Battery Holder
  16-Channel 12-bit PCA9685 PWM/Servo Driver: The Adafruit 16-Channel 12-bit PWM/Servo Driver will drive up to 16 servos over I2C with only 2 pins. The on-board PCA9685 PWM controller will drive all 16 channels simultaneously with no additional processing overhead. What's more, you can chain up to 62 of them to control up to 992 servos - all with the same 2 pins
  DC-DC 2-24V Step Up Booster: Convertisseur DC-DC 2-24V 2A
  H-Bridge with L298N: h-bridge
  LEDs: LEDs Standard schematic elements and footprints for 5mm, 3mm, 1206, and 0603 sized LEDs. 5mm - Spark Fun Electronics SKU : COM-00529 (and others)
